// Logisim project add.circ as structural Verilog: 12 circuits, main circuit half_adder
module main (
);

  latch_8 latch_8_1 ();  // open: Clock, Data, Q
endmodule

module half_adder (
  input  A,
  input  B,
  output S,
  output CO
);

  xor xor_1 (S, A, B);
  and and_1 (CO, A, B);

  // Notes on the sheet:
  //   Half Adder
endmodule

module full_adder (
  input  CI,
  input  A,
  input  B,
  output S,
  output CO
);

  wire half_adder_1_co, half_adder_1_s, half_adder_2_co;

  half_adder half_adder_1 (.A(A), .B(B), .S(half_adder_1_s), .CO(half_adder_1_co));
  half_adder half_adder_2 (.A(CI), .B(half_adder_1_s), .S(S), .CO(half_adder_2_co));
  or or_1 (CO, half_adder_2_co, half_adder_1_co);
endmodule

module adder_8 (
  input  in_1,
  input  in_2,
  input  in_3,
  input  in_4,
  input  in_5,
  input  in_6,
  input  in_7,
  input  in_8,
  input  in_9,
  input  in_10,
  input  in_11,
  input  in_12,
  input  in_13,
  input  in_14,
  input  in_15,
  input  in_16,
  input  in_17,
  output out_18,
  output out_19,
  output out_20,
  output out_21,
  output out_22,
  output out_23,
  output out_24,
  output out_25,
  output out_26
);

  wire full_adder_1_co, full_adder_2_co, full_adder_3_co, full_adder_4_co, full_adder_5_co, full_adder_6_co,
       full_adder_7_co;

  full_adder full_adder_1 (.CI(in_1), .A(in_2), .B(in_3), .S(out_18), .CO(full_adder_1_co));
  full_adder full_adder_2 (.CI(full_adder_1_co), .A(in_4), .B(in_5), .S(out_19), .CO(full_adder_2_co));
  full_adder full_adder_3 (.CI(full_adder_2_co), .A(in_6), .B(in_7), .S(out_20), .CO(full_adder_3_co));
  full_adder full_adder_4 (.CI(full_adder_3_co), .A(in_8), .B(in_9), .S(out_21), .CO(full_adder_4_co));
  full_adder full_adder_5 (.CI(full_adder_4_co), .A(in_10), .B(in_11), .S(out_22), .CO(full_adder_5_co));
  full_adder full_adder_6 (.CI(full_adder_5_co), .A(in_12), .B(in_13), .S(out_23), .CO(full_adder_6_co));
  full_adder full_adder_7 (.CI(full_adder_6_co), .A(in_14), .B(in_15), .S(out_24), .CO(full_adder_7_co));
  full_adder full_adder_8 (.CI(full_adder_7_co), .A(in_16), .B(in_17), .S(out_25), .CO(out_26));
endmodule

module adder_8_bundle (
  input  [7:0] A,
  input  [7:0] B,
  input  CI,
  output CO,
  output [7:0] S
);

  adder_8 adder_8_1 (
    .out_19(S[1]), .out_20(S[2]), .out_21(S[3]), .out_18(S[0]), .out_22(S[4]), .out_23(S[5]), .out_24(S[6]),
    .out_25(S[7]), .out_26(CO), .in_4(A[1]), .in_5(B[1]), .in_6(A[2]), .in_7(B[2]), .in_1(CI), .in_8(A[3]),
    .in_9(B[3]), .in_10(A[4]), .in_11(B[4]), .in_2(A[0]), .in_12(A[5]), .in_13(B[5]), .in_14(A[6]),
    .in_15(B[6]), .in_3(B[0]), .in_16(A[7]), .in_17(B[7]));
endmodule

module adder_16 (
  input  [7:0] A15_A8,
  input  [7:0] B15_B8,
  input  [7:0] A7_A0,
  input  [7:0] B7_B0,
  input  CI,
  output CO,
  output [7:0] S15_S8,
  output [7:0] S7_S0
);

  wire adder_8_bundle_2_co;

  adder_8_bundle adder_8_bundle_1 (.A(A15_A8), .B(B15_B8), .CI(adder_8_bundle_2_co), .CO(CO), .S(S15_S8));
  adder_8_bundle adder_8_bundle_2 (.A(A7_A0), .B(B7_B0), .CI(CI), .CO(adder_8_bundle_2_co), .S(S7_S0));
endmodule

module adder_16_bundle (
  input  [15:0] A,
  input  CI,
  input  [15:0] B,
  output CO,
  output [15:0] S
);

  adder_16 adder_16_1 (
    .A15_A8(A[15:8]), .B15_B8(B[15:8]), .A7_A0(A[15:8]), .B7_B0(B[7:0]), .CI(CI), .CO(CO), .S15_S8(S[15:8]),
    .S7_S0(S[7:0]));

  assign A[7:0] = A[15:8];
endmodule

module rs_flip_flop (
  input  S,
  input  R,
  output Q,
  output Q_not
);

  wire nor_1_out;

  nor nor_1 (nor_1_out, Q, S);
  nor nor_2 (Q, nor_1_out, R);
  not not_1 (Q_not, Q);
endmodule

module lvl_trigg_d_flip_flop (
  input  Clock,
  input  Data,
  output Q,
  output Q_not
);

  wire and_1_out, and_2_out, not_1_out;

  not not_1 (not_1_out, Data);
  and and_1 (and_1_out, Clock, Data);
  and and_2 (and_2_out, Clock, not_1_out);
  rs_flip_flop rs_flip_flop_1 (.S(and_1_out), .R(and_2_out), .Q(Q), .Q_not(Q_not));
endmodule

module latch_8 (
  input  Clock,
  input  [7:0] Data,
  output [7:0] Q
);

  lvl_trigg_d_flip_flop lvl_trigg_d_flip_flop_1 (.Clock(Clock), .Data(Data[0]), .Q(Q[0]));  // open: Q_not
  lvl_trigg_d_flip_flop lvl_trigg_d_flip_flop_2 (.Clock(Clock), .Data(Data[1]), .Q(Q[1]));  // open: Q_not
  lvl_trigg_d_flip_flop lvl_trigg_d_flip_flop_3 (.Clock(Clock), .Data(Data[2]), .Q(Q[2]));  // open: Q_not
  lvl_trigg_d_flip_flop lvl_trigg_d_flip_flop_4 (.Clock(Clock), .Data(Data[3]), .Q(Q[3]));  // open: Q_not
  lvl_trigg_d_flip_flop lvl_trigg_d_flip_flop_5 (.Clock(Clock), .Data(Data[4]), .Q(Q[4]));  // open: Q_not
  lvl_trigg_d_flip_flop lvl_trigg_d_flip_flop_6 (.Clock(Clock), .Data(Data[5]), .Q(Q[5]));  // open: Q_not
  lvl_trigg_d_flip_flop lvl_trigg_d_flip_flop_7 (.Clock(Clock), .Data(Data[6]), .Q(Q[6]));  // open: Q_not
  lvl_trigg_d_flip_flop lvl_trigg_d_flip_flop_8 (.Clock(Clock), .Data(Data[7]), .Q(Q[7]));  // open: Q_not
endmodule

module selector_2_to_1 (
  input  B,
  input  Selector,
  input  A,
  output Q
);

  wire and_1_out, and_2_out, not_1_out;

  not not_1 (not_1_out, Selector);
  and and_1 (and_1_out, B, Selector);
  and and_2 (and_2_out, not_1_out, A);
  or or_1 (Q, and_1_out, and_2_out);
endmodule

module selector8_2_to_1 (
  input  Selector,
  input  [7:0] B,
  input  [7:0] A,
  output [7:0] out_4
);

  selector_2_to_1 selector_2_to_1_1 (.B(B[0]), .Selector(Selector), .A(A[0]), .Q(out_4[0]));
  selector_2_to_1 selector_2_to_1_2 (.B(B[1]), .Selector(Selector), .A(A[1]), .Q(out_4[1]));
  selector_2_to_1 selector_2_to_1_3 (.B(B[2]), .Selector(Selector), .A(A[2]), .Q(out_4[2]));
  selector_2_to_1 selector_2_to_1_4 (.B(B[3]), .Selector(Selector), .A(A[3]), .Q(out_4[3]));
  selector_2_to_1 selector_2_to_1_5 (.B(B[4]), .Selector(Selector), .A(A[4]), .Q(out_4[4]));
  selector_2_to_1 selector_2_to_1_6 (.B(B[5]), .Selector(Selector), .A(A[5]), .Q(out_4[5]));
  selector_2_to_1 selector_2_to_1_7 (.B(B[6]), .Selector(Selector), .A(A[6]), .Q(out_4[6]));
  selector_2_to_1 selector_2_to_1_8 (.B(B[7]), .Selector(Selector), .A(A[7]), .Q(out_4[7]));
endmodule
